// Logisim project Proto1.circ as structural Verilog: 6 circuits, main circuit main
module main (
);

  wire and_1_out, button_1_out, button_2_out, clock_1_out, \fußgrün_1_grün , \fußrot_1_rot ,
       gelbphase_1_gelb, \grünphase_1_grün , or_1_out, rotphase_1_rot;
  wire [4:0] counter_2_q;
  wire [8:0] counter_1_q;

  Clock clock_1 (.out(clock_1_out));
  Counter #(.width(9), .max('h1ff)) counter_1 (
    .count(1'b1), .Q(counter_1_q), .clk(clock_1_out));  // open: load, D, carry, clr
  and and_1 (and_1_out, counter_1_q[0], counter_1_q[1], counter_1_q[2], counter_1_q[3], counter_1_q[4], counter_1_q[5], counter_1_q[6], counter_1_q[7], counter_1_q[8]);
  Counter #(.width(5), .max('h1f)) counter_2 (
    .count(and_1_out), .Q(counter_2_q), .clk(clock_1_out));  // open: load, D, carry, clr
  \GrünPhase  \grünphase_1  (
    .\FünftesBit (counter_2_q[4]), .ViertesBit(counter_2_q[3]), .DrittesBit(counter_2_q[2]),
    .ZweitesBit(counter_2_q[1]), .ErstesBit(counter_2_q[0]), .\Grün (\grünphase_1_grün ));
  GelbPhase gelbphase_1 (
    .\FünftesBit (counter_2_q[4]), .ViertesBit(counter_2_q[3]), .DrittesBit(counter_2_q[2]),
    .ZweitesBit(counter_2_q[1]), .ErstesBit(counter_2_q[0]), .Gelb(gelbphase_1_gelb));
  RotPhase rotphase_1 (
    .\FünftesBit (counter_2_q[4]), .ViertesBit(counter_2_q[3]), .DrittesBit(counter_2_q[2]),
    .ZweitesBit(counter_2_q[1]), .ErstesBit(counter_2_q[0]), .Rot(rotphase_1_rot));
  \FußRot  \fußrot_1  (
    .\FünftesBit (counter_2_q[4]), .ViertesBit(counter_2_q[3]), .DrittesBit(counter_2_q[2]),
    .ZweitesBit(counter_2_q[1]), .ErstesBit(counter_2_q[0]), .Rot(\fußrot_1_rot ));
  LED led_1 (.in(gelbphase_1_gelb));
  LED led_2 (.in(\grünphase_1_grün ));
  \FußGrün  \fußgrün_1  (
    .\FünftesBit (counter_2_q[4]), .ViertesBit(counter_2_q[3]), .DrittesBit(counter_2_q[2]),
    .ZweitesBit(counter_2_q[1]), .ErstesBit(counter_2_q[0]), .\Grün (\fußgrün_1_grün ));
  LED led_3 (.in(rotphase_1_rot));
  LED led_4 (.in(\fußrot_1_rot ));
  LED led_5 (.in(\fußgrün_1_grün ));
  Button button_1 (.out(button_1_out));
  Button button_2 (.out(button_2_out));
  LED led_6 (.in(\fußgrün_1_grün ));
  LED led_7 (.in(\fußrot_1_rot ));
  LED led_8 (.in(rotphase_1_rot));
  LED led_9 (.in(gelbphase_1_gelb));
  LED led_10 (.in(\grünphase_1_grün ));
  or or_1 (or_1_out, button_2_out, button_1_out);

  // Notes on the sheet:
  //   GrünPhase
  //   GelbPhase
  //   RotPhase
  //   FußRot
  //   FußGrün
endmodule

module \GrünPhase  (
  input  \FünftesBit ,
  input  ViertesBit,
  input  DrittesBit,
  input  ZweitesBit,
  input  ErstesBit,
  output \Grün 
);

  wire _0_out, _1_out, _2_out, _3_out, _4_out, _5_out, _6_out, _7_out, _8_out, _9_out, _26_out, _27_out,
       _28_out, _29_out, _30_out, _31_out, not_1_out, not_2_out, not_3_out, not_4_out, not_5_out, not_6_out,
       not_7_out, not_8_out, not_9_out, not_10_out, not_11_out, not_12_out, not_13_out, not_14_out,
       not_15_out, not_16_out, not_17_out, not_18_out, not_19_out, not_20_out, not_21_out, not_22_out,
       not_23_out, not_24_out, not_25_out, not_26_out, not_27_out, not_28_out, not_29_out, not_30_out,
       not_31_out, not_32_out, not_33_out, not_34_out, not_35_out, not_36_out, not_37_out, not_38_out,
       not_39_out, not_40_out, not_41_out, not_42_out, or_1_out, or_2_out;

  not not_1 (not_1_out, ErstesBit);
  not not_2 (not_2_out, ZweitesBit);
  not not_3 (not_3_out, DrittesBit);
  and _0 (_0_out, not_1_out, not_2_out, not_3_out, not_4_out, not_5_out);
  not not_4 (not_4_out, ViertesBit);
  not not_5 (not_5_out, \FünftesBit );
  not not_6 (not_6_out, ZweitesBit);
  not not_7 (not_7_out, DrittesBit);
  and _1 (_1_out, ErstesBit, not_6_out, not_7_out, not_8_out, not_9_out);
  not not_8 (not_8_out, ViertesBit);
  not not_9 (not_9_out, \FünftesBit );
  not not_10 (not_10_out, ErstesBit);
  and _2 (_2_out, not_10_out, ZweitesBit, not_11_out, not_12_out, not_13_out);
  not not_11 (not_11_out, DrittesBit);
  not not_12 (not_12_out, ViertesBit);
  not not_13 (not_13_out, \FünftesBit );
  not not_14 (not_14_out, DrittesBit);
  and _3 (_3_out, ErstesBit, ZweitesBit, not_14_out, not_15_out, not_16_out);
  not not_15 (not_15_out, ViertesBit);
  not not_16 (not_16_out, \FünftesBit );
  not not_17 (not_17_out, ErstesBit);
  not not_18 (not_18_out, ZweitesBit);
  and _4 (_4_out, not_17_out, not_18_out, DrittesBit, not_19_out, not_20_out);
  not not_19 (not_19_out, ViertesBit);
  not not_20 (not_20_out, \FünftesBit );
  not not_21 (not_21_out, ZweitesBit);
  and _5 (_5_out, ErstesBit, not_21_out, DrittesBit, not_22_out, not_23_out);
  not not_22 (not_22_out, ViertesBit);
  not not_23 (not_23_out, \FünftesBit );
  not not_24 (not_24_out, ErstesBit);
  and _6 (_6_out, not_24_out, ZweitesBit, DrittesBit, not_25_out, not_26_out);
  not not_25 (not_25_out, ViertesBit);
  not not_26 (not_26_out, \FünftesBit );
  and _7 (_7_out, ErstesBit, ZweitesBit, DrittesBit, not_27_out, not_28_out);
  not not_27 (not_27_out, ViertesBit);
  not not_28 (not_28_out, \FünftesBit );
  not not_29 (not_29_out, ErstesBit);
  not not_30 (not_30_out, ZweitesBit);
  not not_31 (not_31_out, DrittesBit);
  and _8 (_8_out, not_29_out, not_30_out, not_31_out, ViertesBit, not_32_out);
  not not_32 (not_32_out, \FünftesBit );
  not not_33 (not_33_out, ZweitesBit);
  not not_34 (not_34_out, DrittesBit);
  and _9 (_9_out, ErstesBit, not_33_out, not_34_out, ViertesBit, not_35_out);
  not not_35 (not_35_out, \FünftesBit );
  not not_36 (not_36_out, ErstesBit);
  and _26 (_26_out, not_36_out, ZweitesBit, not_37_out, ViertesBit, \FünftesBit );
  not not_37 (not_37_out, DrittesBit);
  not not_38 (not_38_out, DrittesBit);
  and _27 (_27_out, ErstesBit, ZweitesBit, not_38_out, ViertesBit, \FünftesBit );
  not not_39 (not_39_out, ErstesBit);
  not not_40 (not_40_out, ZweitesBit);
  and _28 (_28_out, not_39_out, not_40_out, DrittesBit, ViertesBit, \FünftesBit );
  not not_41 (not_41_out, ZweitesBit);
  and _29 (_29_out, ErstesBit, not_41_out, DrittesBit, ViertesBit, \FünftesBit );
  not not_42 (not_42_out, ErstesBit);
  and _30 (_30_out, not_42_out, ZweitesBit, DrittesBit, ViertesBit, \FünftesBit );
  and _31 (_31_out, ErstesBit, ZweitesBit, DrittesBit, ViertesBit, \FünftesBit );
  or or_1 (or_1_out, _0_out, _1_out, _2_out, _3_out, _4_out, _5_out, _6_out, _7_out, _8_out, _9_out);
  or or_2 (or_2_out, _26_out, _27_out, _28_out, _29_out, _30_out, _31_out);
  or or_3 (\Grün , or_1_out, or_2_out);
endmodule

module GelbPhase (
  input  \FünftesBit ,
  input  ViertesBit,
  input  DrittesBit,
  input  ZweitesBit,
  input  ErstesBit,
  output Gelb
);

  wire _10_out, _24_out, _25_out, not_1_out, not_2_out, not_3_out, not_4_out, not_5_out, not_6_out,
       not_7_out, not_8_out;

  not not_1 (not_1_out, ErstesBit);
  not not_2 (not_2_out, DrittesBit);
  not not_3 (not_3_out, \FünftesBit );
  not not_4 (not_4_out, ErstesBit);
  not not_5 (not_5_out, ZweitesBit);
  not not_6 (not_6_out, DrittesBit);
  not not_7 (not_7_out, ZweitesBit);
  not not_8 (not_8_out, DrittesBit);
  and _10 (_10_out, not_1_out, ZweitesBit, not_2_out, ViertesBit, not_3_out);
  and _24 (_24_out, not_4_out, not_5_out, not_6_out, ViertesBit, \FünftesBit );
  and _25 (_25_out, ErstesBit, not_7_out, not_8_out, ViertesBit, \FünftesBit );
  or or_1 (Gelb, _10_out, _24_out, _25_out);
endmodule

module RotPhase (
  input  \FünftesBit ,
  input  ViertesBit,
  input  DrittesBit,
  input  ZweitesBit,
  input  ErstesBit,
  output Rot
);

  wire and_1_out, \grünphase_1_grün , not_1_out, not_2_out, not_3_out, not_4_out, not_5_out, or_1_out;

  not not_1 (not_1_out, ErstesBit);
  not not_2 (not_2_out, DrittesBit);
  not not_3 (not_3_out, \FünftesBit );
  \GrünPhase  \grünphase_1  (
    .\FünftesBit (\FünftesBit ), .ViertesBit(ViertesBit), .DrittesBit(DrittesBit), .ZweitesBit(ZweitesBit),
    .ErstesBit(ErstesBit), .\Grün (\grünphase_1_grün ));
  and and_1 (and_1_out, not_1_out, ZweitesBit, not_2_out, ViertesBit, not_3_out);
  or or_1 (or_1_out, ErstesBit, ZweitesBit, DrittesBit, ViertesBit, \FünftesBit );
  not not_4 (not_4_out, \grünphase_1_grün );
  not not_5 (not_5_out, and_1_out);
  and and_2 (Rot, not_4_out, not_5_out, or_1_out);

  // Notes on the sheet:
  //   GrünPhase
  //   GelbPhase
endmodule

module \FußRot  (
  input  \FünftesBit ,
  input  ViertesBit,
  input  DrittesBit,
  input  ZweitesBit,
  input  ErstesBit,
  output Rot
);

  wire _11_out, _12_out, _22_out, _23_out, gelbphase_1_gelb, \grünphase_1_grün , not_1_out, not_2_out,
       not_3_out, not_4_out, not_5_out, not_6_out, not_7_out, not_8_out, or_1_out;

  \GrünPhase  \grünphase_1  (
    .\FünftesBit (\FünftesBit ), .ViertesBit(ViertesBit), .DrittesBit(DrittesBit), .ZweitesBit(ZweitesBit),
    .ErstesBit(ErstesBit), .\Grün (\grünphase_1_grün ));
  GelbPhase gelbphase_1 (
    .\FünftesBit (\FünftesBit ), .ViertesBit(ViertesBit), .DrittesBit(DrittesBit), .ZweitesBit(ZweitesBit),
    .ErstesBit(ErstesBit), .Gelb(gelbphase_1_gelb));
  not not_1 (not_1_out, DrittesBit);
  and _11 (_11_out, ErstesBit, ZweitesBit, not_1_out, ViertesBit, not_2_out);
  not not_2 (not_2_out, \FünftesBit );
  not not_3 (not_3_out, ErstesBit);
  not not_4 (not_4_out, ZweitesBit);
  and _12 (_12_out, not_3_out, not_4_out, DrittesBit, ViertesBit, not_5_out);
  not not_5 (not_5_out, \FünftesBit );
  not not_6 (not_6_out, ErstesBit);
  and _22 (_22_out, not_6_out, ZweitesBit, DrittesBit, not_7_out, \FünftesBit );
  not not_7 (not_7_out, ViertesBit);
  and _23 (_23_out, ErstesBit, ZweitesBit, DrittesBit, not_8_out, \FünftesBit );
  not not_8 (not_8_out, ViertesBit);
  or or_1 (or_1_out, _11_out, _12_out, _22_out, _23_out);
  or or_2 (Rot, \grünphase_1_grün , gelbphase_1_gelb, or_1_out);

  // Notes on the sheet:
  //   GrünPhase
  //   GelbPhase
endmodule

module \FußGrün  (
  input  \FünftesBit ,
  input  ViertesBit,
  input  DrittesBit,
  input  ZweitesBit,
  input  ErstesBit,
  output \Grün 
);

  wire \fußrot_1_rot , not_1_out;

  \FußRot  \fußrot_1  (
    .\FünftesBit (\FünftesBit ), .ViertesBit(ViertesBit), .DrittesBit(DrittesBit), .ZweitesBit(ZweitesBit),
    .ErstesBit(ErstesBit), .Rot(\fußrot_1_rot ));
  not not_1 (not_1_out, \fußrot_1_rot );
  and and_1 (\Grün , not_1_out, 1'b1);
endmodule
